// Logisim project riscv.circ as structural Verilog: 14 circuits, main circuit Control
// ISAriscV
module main (
  output [31:0] out_1
);

  wire ALUSrc, BEQ_EQ, clk, comparator_1_eq, CTRLMUX, ex_mem_1_memtoreg, ex_mem_1_memwrite, EXMEM_WB,
       id_ex_1_branch, id_ex_1_funct7, id_ex_1_memtoreg, id_ex_1_memwrite, IDEX_MEMR, IDEX_WB, IFIDWRITE,
       mem_wb_1_memtoreg, MEMWB_WB, PCWRITE;
  wire [1:0] ALUOp, BEQ_FA, BEQ_FB, control_1_aluop, FA, FB;
  wire [2:0] alucontrol_1_opcode_alu, id_ex_1_funct3;
  wire [4:0] EXMEM_RD, id_ex_1_rs1idex, id_ex_1_rs2idex, IDEX_RD, IFID_RS1, IFID_RS2, MEMWB_RD;
  wire [7:0] multiplexer_5_out;
  wire [7:2] control_1_memwrite;
  wire [23:0] bit_extender_1_out, immgen_1_immpc, multiplexer_1_out, PC, PC_q, PcMaisImm, PcMaisUm,
       shifter_1_out;
  wire [31:0] breg_1_readdata1, breg_1_readdata2, DADO_EXMEM, DadosBREG, ex_mem_1_readdata2, id_ex_1_immalu,
       id_ex_1_readdata1, id_ex_1_readdata2, if_id_1_instruction, immgen_1_immalu, InstructionMemory_data,
       mem_wb_1_aluresult, mem_wb_1_readdatamem, multiplexer_2_out, multiplexer_3_out, multiplexer_4_out,
       multiplexer_6_out, multiplexer_7_out, multiplexer_8_out, ram_1_dout;

  Clock u_clk (.out(clk));
  Multiplexer #(.width(24)) multiplexer_1 (.in0(PcMaisUm), .in1(PcMaisImm), .out(multiplexer_1_out), .sel(BEQ_EQ));
  Register #(.width(24)) u_PC (.D(multiplexer_1_out), .en(PCWRITE), .clk(clk), .Q(PC_q));  // open: clr
  Adder #(.width(24)) adder_1 (.a(PC_q), .b(24'h1), .out(PcMaisUm));  // open: cin, cout
  ROM #(.addrWidth(24), .dataWidth(32)) InstructionMemory (.addr(PC_q), .data(InstructionMemory_data));
  Multiplexer #(.width(32)) multiplexer_2 (
    .in0(InstructionMemory_data), .in1(32'h13), .out(multiplexer_2_out), .sel(CTRLMUX));
  IF_ID if_id_1 (
    .IFID_WRITE(IFIDWRITE), .beq(BEQ_EQ), .PcIn(PC_q), .in_4(multiplexer_2_out), .CLK(clk), .Pc(PC),
    .Instruction({if_id_1_instruction[31:25], IFID_RS2, IFID_RS1, if_id_1_instruction[14:0]}));
  HazardDetection hazarddetection_1 (
    .IDEX_MEMREAD(IDEX_MEMR), .IDEX_RD(IDEX_RD), .IFID_RS1(IFID_RS1), .IDID_RS2(IFID_RS2), .BEQ_EQ(BEQ_EQ),
    .PCWRITE(PCWRITE), .IFID_WRITE(IFIDWRITE), .ControlMUX(CTRLMUX));
  Control control_1 (
    .Instruction(if_id_1_instruction[6:0]), .ALUOp(control_1_aluop), .MemWrite(control_1_memwrite[2]),
    .Branch(control_1_memwrite[3]), .MemToReg(control_1_memwrite[4]), .MemRead(control_1_memwrite[5]),
    .RegWrite(control_1_memwrite[6]), .ALUSrc(control_1_memwrite[7]));
  ImmGen immgen_1 (
    .Instruction({if_id_1_instruction[31:25], IFID_RS2, IFID_RS1, if_id_1_instruction[14:0]}),
    .ImmPC(immgen_1_immpc), .ImmALU(immgen_1_immalu));
  BReg breg_1 (
    .ReadRegister1(IFID_RS1), .ReadRegister2(IFID_RS2), .WriteData(DadosBREG), .RegWrite(MEMWB_WB),
    .WriteRegister(MEMWB_RD), .ReadData1(breg_1_readdata1), .ReadData2(breg_1_readdata2));
  FordUnitBEQ fordunitbeq_1 (
    .IDEX_RD(IDEX_RD), .IDEX_REGWRITE(IDEX_WB), .IFID_RS1(IFID_RS1), .IFID_RS2(IFID_RS2),
    .EXMEM_RD(EXMEM_RD), .EXMEM_REGWRITE(EXMEM_WB), .ForwardA(BEQ_FA), .ForwardB(BEQ_FB));
  Multiplexer #(.select(2), .width(32)) multiplexer_3 (
    .in0(breg_1_readdata1), .in1(DADO_EXMEM), .in2(out_1), .out(multiplexer_3_out), .sel(BEQ_FA));  // open: in3
  Multiplexer #(.select(2), .width(32)) multiplexer_4 (
    .in0(breg_1_readdata2), .in1(DADO_EXMEM), .in2(out_1), .out(multiplexer_4_out), .sel(BEQ_FB));  // open: in3
  Shifter #(.shift("ar"), .width(24)) shifter_1 (.in(immgen_1_immpc), .\dist (5'b00010), .out(shifter_1_out));
  Comparator #(.width(32)) comparator_1 (
    .a(multiplexer_3_out), .b(multiplexer_4_out), .eq(comparator_1_eq));  // open: gt, lt
  Adder #(.width(24)) adder_2 (.a(PC), .b(shifter_1_out), .out(PcMaisImm));  // open: cin, cout
  Multiplexer #(.width(8)) multiplexer_5 (
    .in0({control_1_memwrite, control_1_aluop}), .in1({8{1'b0}}), .out(multiplexer_5_out), .sel(CTRLMUX));
  and and_1 (BEQ_EQ, control_1_memwrite[3], comparator_1_eq);
  ID_EX id_ex_1 (
    .CLK(clk), .ReadData1In(breg_1_readdata1), .ReadData2In(breg_1_readdata2),
    .ALUOpIn(multiplexer_5_out[1:0]), .ImmALUIn(immgen_1_immalu), .Funct7In(if_id_1_instruction[30]),
    .Funct3In(if_id_1_instruction[14:12]), .WriteRegisterIn(if_id_1_instruction[11:7]), .RS1(IFID_RS1),
    .MemWriteIn(multiplexer_5_out[2]), .BranchIn(multiplexer_5_out[3]), .MemToRegIn(multiplexer_5_out[4]),
    .MemReadIn(multiplexer_5_out[5]), .RegWriteIn(multiplexer_5_out[6]), .ALUSrcIn(multiplexer_5_out[7]),
    .RS2(IFID_RS2), .ReadData1(id_ex_1_readdata1), .ReadData2(id_ex_1_readdata2), .ALUOp(ALUOp),
    .ImmALU(id_ex_1_immalu), .Funct7(id_ex_1_funct7), .Funct3(id_ex_1_funct3), .WriteRegister(IDEX_RD),
    .RS1IDEX(id_ex_1_rs1idex), .RS2IDEX(id_ex_1_rs2idex), .MemWrite(id_ex_1_memwrite),
    .Branch(id_ex_1_branch), .MemToReg(id_ex_1_memtoreg), .MemRead(IDEX_MEMR), .RegWrite(IDEX_WB),
    .ALUSrc(ALUSrc));
  Multiplexer #(.select(2), .width(32)) multiplexer_6 (
    .in0(id_ex_1_readdata2), .in1(DadosBREG), .in2(DADO_EXMEM), .out(multiplexer_6_out), .sel(FB));  // open: in3
  Multiplexer #(.select(2), .width(32)) multiplexer_7 (
    .in0(id_ex_1_readdata1), .in1(DadosBREG), .in2(DADO_EXMEM), .out(multiplexer_7_out), .sel(FA));  // open: in3
  FordUnit fordunit_1 (
    .EXMEM_RD(EXMEM_RD), .EXMEM_REGWRITE(EXMEM_WB), .IDEX_RS1(id_ex_1_rs1idex), .IDEX_RS2(id_ex_1_rs2idex),
    .MEMWB_RD(MEMWB_RD), .MEMWB_REGWRITE(MEMWB_WB), .ForwardA(FA), .ForwardB(FB));
  Multiplexer #(.width(32)) multiplexer_8 (
    .in0(multiplexer_6_out), .in1(id_ex_1_immalu), .out(multiplexer_8_out), .sel(ALUSrc));
  ALU alu_1 (
    .MemWrite(id_ex_1_memwrite), .MemRead(IDEX_MEMR), .RS1(multiplexer_7_out),
    .OpcodeALU(alucontrol_1_opcode_alu), .RS2orIMM(multiplexer_8_out), .Dado(out_1));
  ALUControl alucontrol_1 (
    .ALUOp(ALUOp), .Funct7Bit5(id_ex_1_funct7), .Funct3(id_ex_1_funct3), .Opcode_ALU(alucontrol_1_opcode_alu));
  EX_MEM ex_mem_1 (
    .CLK(clk), .ReadData2In(multiplexer_6_out), .ALUResultIn(out_1), .WriteRegisterIn(IDEX_RD),
    .MemWriteIn(id_ex_1_memwrite), .MemToRegIn(id_ex_1_memtoreg), .RegWriteIn(IDEX_WB),
    .ReadData2(ex_mem_1_readdata2), .ALUResult(DADO_EXMEM), .WriteRegister(EXMEM_RD),
    .MemWrite(ex_mem_1_memwrite), .MemToReg(ex_mem_1_memtoreg), .RegWrite(EXMEM_WB));
  Bit_Extender #(.in_width(32), .out_width(24), .\type ("zero")) bit_extender_1 (
    .in(DADO_EXMEM), .out(bit_extender_1_out));
  RAM #(.addrWidth(24), .dataWidth(32)) ram_1 (
    .addr(bit_extender_1_out), .we(ex_mem_1_memwrite), .oe(1'b1), .clk(clk), .din(ex_mem_1_readdata2),
    .dout(ram_1_dout));
  MEM_WB mem_wb_1 (
    .CLK(clk), .ReadDataMemIn(ram_1_dout), .ALUResultIn(DADO_EXMEM), .WriteRegisterIn(EXMEM_RD),
    .MemToRegIn(ex_mem_1_memtoreg), .RegWriteIn(EXMEM_WB), .ReadDataMem(mem_wb_1_readdatamem),
    .ALUResult(mem_wb_1_aluresult), .WriteRegister(MEMWB_RD), .MemToReg(mem_wb_1_memtoreg),
    .RegWrite(MEMWB_WB));
  Multiplexer #(.width(32)) multiplexer_9 (
    .in0(mem_wb_1_aluresult), .in1(mem_wb_1_readdatamem), .out(DadosBREG), .sel(mem_wb_1_memtoreg));

  // Other names for the same wires on the sheet: DADO_IDEX[31:0] = out_1; RegWrite = MEMWB_WB;
  //   WriteRegister[4:0] = MEMWB_RD
endmodule

module Control (
  input  [6:0] Instruction,
  output [1:0] ALUOp,
  output MemWrite,
  output Branch,
  output MemToReg,
  output MemRead,
  output RegWrite,
  output ALUSrc
);

  wire and_1_out, and_2_out, and_3_out, and_4_out, not_1_out, not_2_out, not_3_out, not_4_out, not_5_out,
       not_6_out, not_7_out, not_8_out, not_9_out, or_1_out;

  not not_1 (not_1_out, Instruction[6]);
  and and_1 (and_1_out, Instruction[4], not_1_out, not_2_out);
  not not_2 (not_2_out, Instruction[5]);
  not not_3 (not_3_out, Instruction[4]);
  not not_4 (not_4_out, Instruction[6]);
  not not_5 (not_5_out, Instruction[5]);
  and and_2 (and_2_out, not_3_out, Instruction[5], not_4_out);
  not not_6 (not_6_out, Instruction[5]);
  and and_3 (and_3_out, not_6_out, not_7_out);
  not not_7 (not_7_out, Instruction[4]);
  not not_8 (not_8_out, Instruction[4]);
  and and_4 (and_4_out, not_8_out, Instruction[5]);
  or or_1 (or_1_out, not_5_out, and_2_out);
  or or_2 (ALUOp[0], and_1_out, Instruction[6]);
  not not_9 (not_9_out, and_4_out);
  and and_5 (Branch, Instruction[0], Instruction[6]);
  and and_6 (MemToReg, and_3_out, Instruction[0]);
  and and_7 (MemRead, and_3_out, Instruction[0]);
  and and_8 (RegWrite, not_9_out, Instruction[0]);
  and and_9 (ALUSrc, or_1_out, Instruction[0]);
  and and_10 (MemWrite, and_2_out, Instruction[0]);
  nor nor_1 (ALUOp[1], and_3_out, Instruction[6], and_2_out);

  // Other names for the same wires on the sheet: opcode0 = Instruction[0]
endmodule

module ALU (
  input  MemWrite,
  input  MemRead,
  input  [31:0] RS1,
  input  [2:0] OpcodeALU,
  input  [31:0] RS2orIMM,
  output [31:0] Dado
);

  wire or_1_out;
  wire [31:0] adder_1_out, and_1_out, multiplexer_1_out, multiplexer_2_out, or_2_out, shifter_1_out,
       shifter_2_out, shifter_3_out, subtractor_1_out;

  or or_1 (or_1_out, MemWrite, MemRead);
  Shifter #(.shift("ar"), .width(32)) shifter_1 (.in(RS1), .\dist (5'b00010), .out(shifter_1_out));
  Shifter #(.shift("ar"), .width(32)) shifter_2 (.in(RS2orIMM), .\dist (5'b00010), .out(shifter_2_out));
  Multiplexer #(.width(32)) multiplexer_1 (.in0(RS1), .in1(shifter_1_out), .out(multiplexer_1_out), .sel(or_1_out));
  Multiplexer #(.width(32)) multiplexer_2 (
    .in0(RS2orIMM), .in1(shifter_2_out), .out(multiplexer_2_out), .sel(or_1_out));
  Subtractor #(.width(32)) subtractor_1 (.a(RS1), .b(RS2orIMM), .out(subtractor_1_out));  // open: bin, bout
  Adder #(.width(32)) adder_1 (.a(multiplexer_1_out), .b(multiplexer_2_out), .out(adder_1_out));  // open: cin, cout
  assign and_1_out = RS1 & RS2orIMM;  // AND_Gate and_1, 32 bits wide
  assign or_2_out = RS1 | RS2orIMM;  // OR_Gate or_2, 32 bits wide
  Shifter #(.width(32)) shifter_3 (.in(RS1), .\dist (RS2orIMM[4:0]), .out(shifter_3_out));
  Multiplexer #(.select(3), .width(32)) multiplexer_3 (
    .in0(adder_1_out), .in1(subtractor_1_out), .in3(and_1_out), .in4(or_2_out), .in5(shifter_3_out),
    .out(Dado), .sel(OpcodeALU));  // open: in2, in6, in7
endmodule

module BReg (
  input  [4:0] ReadRegister1,
  input  [4:0] ReadRegister2,
  input  [31:0] WriteData,
  input  RegWrite,
  input  [4:0] WriteRegister,
  output [31:0] ReadData1,
  output [31:0] ReadData2
);

  wire clk, demultiplexer_1_out0, w1, w2, w3, w4, w5, w6, w7, w8, w9, w10, w11, w12, w13, w14, w15, w16, w17,
       w18, w19, w20, w21, w22, w23, w24, w25, w26, w27, w28, w29, w30, w31;
  wire [31:0] DadoX1, DadoX2, DadoX3, DadoX4, DadoX5, DadoX6, DadoX7, DadoX8, DadoX9, DadoX10, DadoX11,
       DadoX12, DadoX13, DadoX14, DadoX15, DadoX16, DadoX17, DadoX18, DadoX19, DadoX20, DadoX21, DadoX22,
       DadoX23, DadoX24, DadoX25, DadoX26, DadoX27, DadoX28, DadoX29, DadoX30, DadoX31;

  Clock u_clk (.out(clk));
  Demultiplexer #(.select(5)) demultiplexer_1 (
    .out0(demultiplexer_1_out0), .out1(w1), .out2(w2), .out3(w3), .out4(w4), .out5(w5), .out6(w6), .out7(w7),
    .out8(w8), .out9(w9), .out10(w10), .out11(w11), .out12(w12), .out13(w13), .out14(w14), .out15(w15),
    .out16(w16), .out17(w17), .out18(w18), .out19(w19), .out20(w20), .out21(w21), .out22(w22), .out23(w23),
    .out24(w24), .out25(w25), .out26(w26), .out27(w27), .out28(w28), .out29(w29), .out30(w30), .out31(w31),
    .in(RegWrite), .sel(WriteRegister));
  Register #(.width(32)) RA (.D(WriteData), .en(w1), .clk(clk), .Q(DadoX1));  // open: clr
  Register #(.width(32)) SP (.D(WriteData), .en(w2), .clk(clk), .Q(DadoX2));  // open: clr
  Register #(.width(32)) GP (.D(WriteData), .en(w3), .clk(clk), .Q(DadoX3));  // open: clr
  Register #(.width(32)) TP (.D(WriteData), .en(w4), .clk(clk), .Q(DadoX4));  // open: clr
  Register #(.width(32)) t0 (.D(WriteData), .en(w5), .clk(clk), .Q(DadoX5));  // open: clr
  Register #(.width(32)) t1 (.D(WriteData), .en(w6), .clk(clk), .Q(DadoX6));  // open: clr
  Register #(.width(32)) t2 (.D(WriteData), .en(w7), .clk(clk), .Q(DadoX7));  // open: clr
  Register #(.width(32)) s0fp (.D(WriteData), .en(w8), .clk(clk), .Q(DadoX8));  // open: clr
  Register #(.width(32)) s1 (.D(WriteData), .en(w9), .clk(clk), .Q(DadoX9));  // open: clr
  Register #(.width(32)) a0 (.D(WriteData), .en(w10), .clk(clk), .Q(DadoX10));  // open: clr
  Register #(.width(32)) a1 (.D(WriteData), .en(w11), .clk(clk), .Q(DadoX11));  // open: clr
  Register #(.width(32)) a2 (.D(WriteData), .en(w12), .clk(clk), .Q(DadoX12));  // open: clr
  Register #(.width(32)) a3 (.D(WriteData), .en(w13), .clk(clk), .Q(DadoX13));  // open: clr
  Register #(.width(32)) a4 (.D(WriteData), .en(w14), .clk(clk), .Q(DadoX14));  // open: clr
  Register #(.width(32)) a5 (.D(WriteData), .en(w15), .clk(clk), .Q(DadoX15));  // open: clr
  Register #(.width(32)) a6 (.D(WriteData), .en(w16), .clk(clk), .Q(DadoX16));  // open: clr
  Register #(.width(32)) a7 (.D(WriteData), .en(w17), .clk(clk), .Q(DadoX17));  // open: clr
  Register #(.width(32)) s2 (.D(WriteData), .en(w18), .clk(clk), .Q(DadoX18));  // open: clr
  Register #(.width(32)) s3 (.D(WriteData), .en(w19), .clk(clk), .Q(DadoX19));  // open: clr
  Register #(.width(32)) s4 (.D(WriteData), .en(w20), .clk(clk), .Q(DadoX20));  // open: clr
  Register #(.width(32)) s5 (.D(WriteData), .en(w21), .clk(clk), .Q(DadoX21));  // open: clr
  Register #(.width(32)) s6 (.D(WriteData), .en(w22), .clk(clk), .Q(DadoX22));  // open: clr
  Register #(.width(32)) s7 (.D(WriteData), .en(w23), .clk(clk), .Q(DadoX23));  // open: clr
  Register #(.width(32)) s8 (.D(WriteData), .en(w24), .clk(clk), .Q(DadoX24));  // open: clr
  Register #(.width(32)) s9 (.D(WriteData), .en(w25), .clk(clk), .Q(DadoX25));  // open: clr
  Register #(.width(32)) s10 (.D(WriteData), .en(w26), .clk(clk), .Q(DadoX26));  // open: clr
  Register #(.width(32)) s11 (.D(WriteData), .en(w27), .clk(clk), .Q(DadoX27));  // open: clr
  Register #(.width(32)) t3 (.D(WriteData), .en(w28), .clk(clk), .Q(DadoX28));  // open: clr
  Register #(.width(32)) t4 (.D(WriteData), .en(w29), .clk(clk), .Q(DadoX29));  // open: clr
  Register #(.width(32)) t5 (.D(WriteData), .en(w30), .clk(clk), .Q(DadoX30));  // open: clr
  Register #(.width(32)) t6 (.D(WriteData), .en(w31), .clk(clk), .Q(DadoX31));  // open: clr
  Multiplexer #(.select(5), .width(32)) multiplexer_1 (
    .in0({32{1'b0}}), .in1(DadoX1), .in2(DadoX2), .in3(DadoX3), .in4(DadoX4), .in5(DadoX5), .in6(DadoX6),
    .in7(DadoX7), .in8(DadoX8), .in9(DadoX9), .in10(DadoX10), .in11(DadoX11), .in12(DadoX12), .in13(DadoX13),
    .in14(DadoX14), .in15(DadoX15), .in16(DadoX16), .in17(DadoX17), .in18(DadoX18), .in19(DadoX19),
    .in20(DadoX20), .in21(DadoX21), .in22(DadoX22), .in23(DadoX23), .in24(DadoX24), .in25(DadoX25),
    .in26(DadoX26), .in27(DadoX27), .in28(DadoX28), .in29(DadoX29), .in30(DadoX30), .in31(DadoX31),
    .out(ReadData1), .sel(ReadRegister1));
  Multiplexer #(.select(5), .width(32)) multiplexer_2 (
    .in0({32{1'b0}}), .in1(DadoX1), .in2(DadoX2), .in3(DadoX3), .in4(DadoX4), .in5(DadoX5), .in6(DadoX6),
    .in7(DadoX7), .in8(DadoX8), .in9(DadoX9), .in10(DadoX10), .in11(DadoX11), .in12(DadoX12), .in13(DadoX13),
    .in14(DadoX14), .in15(DadoX15), .in16(DadoX16), .in17(DadoX17), .in18(DadoX18), .in19(DadoX19),
    .in20(DadoX20), .in21(DadoX21), .in22(DadoX22), .in23(DadoX23), .in24(DadoX24), .in25(DadoX25),
    .in26(DadoX26), .in27(DadoX27), .in28(DadoX28), .in29(DadoX29), .in30(DadoX30), .in31(DadoX31),
    .out(ReadData2), .sel(ReadRegister2));

  // Other names for the same wires on the sheet: Dado[31:0] = WriteData; EndRS1[4:0] = ReadRegister1;
  //   EndRS2[4:0] = ReadRegister2
endmodule

module ALUControl (
  input  [1:0] ALUOp,
  input  Funct7Bit5,
  input  [2:0] Funct3,
  output [2:0] Opcode_ALU
);

  wire and_1_out, and_2_out, and_3_out, and_4_out, and_5_out, and_6_out, and_7_out, and_8_out, and_9_out,
       and_11_out, and_12_out, not_1_out, not_2_out, not_3_out, not_4_out, not_5_out, not_6_out, not_7_out,
       not_8_out, not_9_out, not_10_out, not_11_out;

  and and_1 (and_1_out, ALUOp[0], not_1_out);
  not not_1 (not_1_out, ALUOp[1]);
  not not_2 (not_2_out, ALUOp[0]);
  not not_3 (not_3_out, Funct3[0]);
  not not_4 (not_4_out, Funct3[1]);
  not not_5 (not_5_out, Funct3[2]);
  not not_6 (not_6_out, ALUOp[0]);
  not not_7 (not_7_out, Funct7Bit5);
  not not_8 (not_8_out, Funct7Bit5);
  not not_9 (not_9_out, Funct3[1]);
  not not_10 (not_10_out, Funct3[2]);
  not not_11 (not_11_out, Funct3[0]);
  and and_2 (and_2_out, not_2_out, ALUOp[1], Funct7Bit5);
  and and_3 (and_3_out, not_3_out, not_4_out, not_5_out);
  and and_4 (and_4_out, not_6_out, ALUOp[1], not_7_out);
  and and_5 (and_5_out, Funct3[0], Funct3[1], Funct3[2]);
  and and_6 (and_6_out, ALUOp[0], ALUOp[1], not_8_out);
  and and_7 (and_7_out, Funct3[0], not_9_out, not_10_out);
  and and_8 (and_8_out, not_11_out, Funct3[1], Funct3[2]);
  and and_9 (and_9_out, and_2_out, and_3_out);
  and and_10 (Opcode_ALU[1], and_4_out, and_5_out);
  and and_11 (and_11_out, and_6_out, and_7_out);
  and and_12 (and_12_out, and_4_out, and_8_out);
  or or_1 (Opcode_ALU[0], and_1_out, and_9_out, Opcode_ALU[1], and_11_out);
  or or_2 (Opcode_ALU[2], and_11_out, and_12_out);

  // Other names for the same wires on the sheet: c0 = Opcode_ALU[0]; c1 = Opcode_ALU[1]; c3 = Opcode_ALU[2]
endmodule

module ImmGen (
  input  [31:0] Instruction,
  output [23:0] ImmPC,
  output [31:0] ImmALU
);

  wire and_1_out;
  wire [31:0] bit_extender_1_out, bit_extender_2_out;

  and and_1 (and_1_out, Instruction[0], Instruction[5], Instruction[1]);
  assign bit_extender_1_out = {{20{Instruction[31]}}, Instruction[31:20]};  // Bit_Extender bit_extender_1
  assign bit_extender_2_out = {{20{Instruction[31]}}, {Instruction[31:25], Instruction[11:7]}};  // Bit_Extender bit_extender_2
  assign ImmPC = {{11{Instruction[31]}}, {Instruction[31], Instruction[7], Instruction[30:25], Instruction[11:8], 1'b0}};  // Bit_Extender bit_extender_3
  Multiplexer #(.width(32)) multiplexer_1 (
    .in0(bit_extender_1_out), .in1(bit_extender_2_out), .out(ImmALU), .sel(and_1_out));
endmodule

module IF_ID (
  input  [23:0] PcIn,
  input  beq,
  input  IFID_WRITE,
  input  [31:0] in_4,
  input  CLK,
  output [23:0] Pc,
  output [31:0] Instruction
);

  wire or_1_out, or_2_out;

  or or_1 (or_1_out, beq, IFID_WRITE);
  or or_2 (or_2_out, beq, IFID_WRITE);
  Register #(.width(24)) register_1 (.D(PcIn), .en(or_1_out), .clk(CLK), .Q(Pc));  // open: clr
  Register #(.width(32)) register_2 (.D(in_4), .en(or_2_out), .clk(CLK), .Q(Instruction));  // open: clr
endmodule

module ID_EX (
  input  [1:0] ALUOpIn,
  input  MemWriteIn,
  input  BranchIn,
  input  MemToRegIn,
  input  MemReadIn,
  input  RegWriteIn,
  input  ALUSrcIn,
  input  [31:0] ReadData1In,
  input  [31:0] ReadData2In,
  input  CLK,
  input  [31:0] ImmALUIn,
  input  Funct7In,
  input  [2:0] Funct3In,
  input  [4:0] WriteRegisterIn,
  input  [4:0] RS1,
  input  [4:0] RS2,
  output [1:0] ALUOp,
  output MemWrite,
  output Branch,
  output MemToReg,
  output MemRead,
  output RegWrite,
  output ALUSrc,
  output [31:0] ReadData1,
  output [31:0] ReadData2,
  output [31:0] ImmALU,
  output Funct7,
  output [2:0] Funct3,
  output [4:0] WriteRegister,
  output [4:0] RS1IDEX,
  output [4:0] RS2IDEX
);

  Register #(.width(2)) register_1 (.D(ALUOpIn), .en(1'b1), .clk(CLK), .Q(ALUOp));  // open: clr
  Register #(.width(1)) register_2 (.D(MemWriteIn), .en(1'b1), .clk(CLK), .Q(MemWrite));  // open: clr
  Register #(.width(1)) register_3 (.D(BranchIn), .en(1'b1), .clk(CLK), .Q(Branch));  // open: clr
  Register #(.width(1)) register_4 (.D(MemToRegIn), .en(1'b1), .clk(CLK), .Q(MemToReg));  // open: clr
  Register #(.width(1)) register_5 (.D(MemReadIn), .en(1'b1), .clk(CLK), .Q(MemRead));  // open: clr
  Register #(.width(1)) register_6 (.D(RegWriteIn), .en(1'b1), .clk(CLK), .Q(RegWrite));  // open: clr
  Register #(.width(1)) register_7 (.D(ALUSrcIn), .en(1'b1), .clk(CLK), .Q(ALUSrc));  // open: clr
  Register #(.width(32)) register_8 (.D(ReadData1In), .en(1'b1), .clk(CLK), .Q(ReadData1));  // open: clr
  Register #(.width(32)) register_9 (.D(ReadData2In), .en(1'b1), .clk(CLK), .Q(ReadData2));  // open: clr
  Register #(.width(32)) register_10 (.D(ImmALUIn), .en(1'b1), .clk(CLK), .Q(ImmALU));  // open: clr
  Register #(.width(1)) register_11 (.D(Funct7In), .en(1'b1), .clk(CLK), .Q(Funct7));  // open: clr
  Register #(.width(3)) register_12 (.D(Funct3In), .en(1'b1), .clk(CLK), .Q(Funct3));  // open: clr
  Register #(.width(5)) register_13 (.D(WriteRegisterIn), .en(1'b1), .clk(CLK), .Q(WriteRegister));  // open: clr
  Register #(.width(5)) register_14 (.D(RS1), .en(1'b1), .clk(CLK), .Q(RS1IDEX));  // open: clr
  Register #(.width(5)) register_15 (.D(RS2), .en(1'b1), .clk(CLK), .Q(RS2IDEX));  // open: clr
endmodule

module EX_MEM (
  input  MemWriteIn,
  input  MemToRegIn,
  input  RegWriteIn,
  input  [31:0] ReadData2In,
  input  CLK,
  input  [31:0] ALUResultIn,
  input  [4:0] WriteRegisterIn,
  output MemWrite,
  output MemToReg,
  output RegWrite,
  output [31:0] ReadData2,
  output [31:0] ALUResult,
  output [4:0] WriteRegister
);

  Register #(.width(1)) register_1 (.D(MemWriteIn), .en(1'b1), .clk(CLK), .Q(MemWrite));  // open: clr
  Register #(.width(1)) register_2 (.D(MemToRegIn), .en(1'b1), .clk(CLK), .Q(MemToReg));  // open: clr
  Register #(.width(1)) register_3 (.D(RegWriteIn), .en(1'b1), .clk(CLK), .Q(RegWrite));  // open: clr
  Register #(.width(32)) register_4 (.D(ReadData2In), .en(1'b1), .clk(CLK), .Q(ReadData2));  // open: clr
  Register #(.width(32)) register_5 (.D(ALUResultIn), .en(1'b1), .clk(CLK), .Q(ALUResult));  // open: clr
  Register #(.width(5)) register_6 (.D(WriteRegisterIn), .en(1'b1), .clk(CLK), .Q(WriteRegister));  // open: clr
endmodule

module MEM_WB (
  input  MemToRegIn,
  input  RegWriteIn,
  input  [31:0] ReadDataMemIn,
  input  CLK,
  input  [31:0] ALUResultIn,
  input  [4:0] WriteRegisterIn,
  output MemToReg,
  output RegWrite,
  output [31:0] ReadDataMem,
  output [31:0] ALUResult,
  output [4:0] WriteRegister
);

  Register #(.width(1)) register_1 (.D(MemToRegIn), .en(1'b1), .clk(CLK), .Q(MemToReg));  // open: clr
  Register #(.width(1)) register_2 (.D(RegWriteIn), .en(1'b1), .clk(CLK), .Q(RegWrite));  // open: clr
  Register #(.width(32)) register_3 (.D(ReadDataMemIn), .en(1'b1), .clk(CLK), .Q(ReadDataMem));  // open: clr
  Register #(.width(32)) register_4 (.D(ALUResultIn), .en(1'b1), .clk(CLK), .Q(ALUResult));  // open: clr
  Register #(.width(5)) register_5 (.D(WriteRegisterIn), .en(1'b1), .clk(CLK), .Q(WriteRegister));  // open: clr
endmodule

module HazardDetection (
  input  IDEX_MEMREAD,
  input  [4:0] IDEX_RD,
  input  [4:0] IFID_RS1,
  input  [4:0] IDID_RS2,
  input  BEQ_EQ,
  output PCWRITE,
  output IFID_WRITE,
  output ControlMUX
);

  wire and_1_out, comparator_1_eq, comparator_2_eq, mux, or_1_out, xor_1_out;

  Comparator #(.width(5)) comparator_1 (.a(IDEX_RD), .b(IFID_RS1), .eq(comparator_1_eq));  // open: gt, lt
  Comparator #(.width(5)) comparator_2 (.a(IDEX_RD), .b(IDID_RS2), .eq(comparator_2_eq));  // open: gt, lt
  or or_1 (or_1_out, comparator_1_eq, comparator_2_eq);
  and and_1 (and_1_out, IDEX_MEMREAD, or_1_out);
  or or_2 (mux, and_1_out, BEQ_EQ);
  Multiplexer multiplexer_1 (.in0(1'b1), .in1(1'b0), .out(PCWRITE), .sel(xor_1_out));
  xor xor_1 (xor_1_out, mux, BEQ_EQ);
  Multiplexer multiplexer_2 (.in0(1'b1), .in1(1'b0), .out(IFID_WRITE), .sel(mux));
  Multiplexer multiplexer_3 (.in0(1'b0), .in1(1'b1), .out(ControlMUX), .sel(mux));

  // Other names for the same wires on the sheet: beq = BEQ_EQ
endmodule

module FordUnit (
  input  [4:0] EXMEM_RD,
  input  EXMEM_REGWRITE,
  input  [4:0] IDEX_RS1,
  input  [4:0] IDEX_RS2,
  input  [4:0] MEMWB_RD,
  input  MEMWB_REGWRITE,
  output [1:0] ForwardA,
  output [1:0] ForwardB
);

  wire and_1_out, and_2_out, and_5_out, and_6_out, comparator_1_eq, comparator_2_eq, comparator_3_eq,
       comparator_4_eq, comparator_5_eq, comparator_6_eq, FA01, FA10, FB01, FB10, not_1_out, not_2_out, notA,
       notB;

  Comparator #(.width(5)) comparator_1 (.a(EXMEM_RD), .b({5{1'b0}}), .eq(comparator_1_eq));  // open: gt, lt
  Comparator #(.width(5)) comparator_2 (.a(EXMEM_RD), .b(IDEX_RS1), .eq(comparator_2_eq));  // open: gt, lt
  Comparator #(.width(5)) comparator_3 (.a(EXMEM_RD), .b(IDEX_RS2), .eq(comparator_3_eq));  // open: gt, lt
  not not_1 (not_1_out, comparator_4_eq);
  Comparator #(.width(5)) comparator_4 (.a(MEMWB_RD), .b({5{1'b0}}), .eq(comparator_4_eq));  // open: gt, lt
  Comparator #(.width(5)) comparator_5 (.a(MEMWB_RD), .b(IDEX_RS1), .eq(comparator_5_eq));  // open: gt, lt
  Comparator #(.width(5)) comparator_6 (.a(MEMWB_RD), .b(IDEX_RS2), .eq(comparator_6_eq));  // open: gt, lt
  not not_2 (not_2_out, comparator_1_eq);
  and and_1 (and_1_out, not_2_out, EXMEM_REGWRITE);
  and and_2 (and_2_out, not_1_out, MEMWB_REGWRITE);
  and and_3 (FA10, and_1_out, comparator_2_eq);
  and and_4 (FB10, and_1_out, comparator_3_eq);
  and and_5 (and_5_out, and_2_out, notA);
  and and_6 (and_6_out, and_2_out, notB);
  and and_7 (FA01, and_5_out, comparator_5_eq);
  and and_8 (FB01, and_6_out, comparator_6_eq);
  not not_3 (notA, FA10);
  not not_4 (notB, FB10);
  Multiplexer multiplexer_1 (.in0(1'b0), .in1(1'b1), .out(ForwardA[0]), .sel(FA01));
  Multiplexer multiplexer_2 (.in0(1'b0), .in1(1'b1), .out(ForwardA[1]), .sel(FA10));
  Multiplexer multiplexer_3 (.in0(1'b0), .in1(1'b1), .out(ForwardB[0]), .sel(FB01));
  Multiplexer multiplexer_4 (.in0(1'b0), .in1(1'b1), .out(ForwardB[1]), .sel(FB10));
endmodule

module FordUnitBEQ (
  input  [4:0] IDEX_RD,
  input  IDEX_REGWRITE,
  input  [4:0] IFID_RS1,
  input  [4:0] IFID_RS2,
  input  [4:0] EXMEM_RD,
  input  EXMEM_REGWRITE,
  output [1:0] ForwardA,
  output [1:0] ForwardB
);

  wire and_1_out, and_2_out, and_5_out, and_6_out, comparator_1_eq, comparator_2_eq, comparator_3_eq,
       comparator_4_eq, comparator_5_eq, comparator_6_eq, FA01, FA10, FB01, FB10, not_1_out, not_2_out, notA,
       notB;

  Comparator #(.width(5)) comparator_1 (.a(IDEX_RD), .b({5{1'b0}}), .eq(comparator_1_eq));  // open: gt, lt
  Comparator #(.width(5)) comparator_2 (.a(IDEX_RD), .b(IFID_RS1), .eq(comparator_2_eq));  // open: gt, lt
  Comparator #(.width(5)) comparator_3 (.a(IDEX_RD), .b(IFID_RS2), .eq(comparator_3_eq));  // open: gt, lt
  not not_1 (not_1_out, comparator_4_eq);
  Comparator #(.width(5)) comparator_4 (.a(EXMEM_RD), .b({5{1'b0}}), .eq(comparator_4_eq));  // open: gt, lt
  Comparator #(.width(5)) comparator_5 (.a(EXMEM_RD), .b(IFID_RS1), .eq(comparator_5_eq));  // open: gt, lt
  Comparator #(.width(5)) comparator_6 (.a(EXMEM_RD), .b(IFID_RS2), .eq(comparator_6_eq));  // open: gt, lt
  not not_2 (not_2_out, comparator_1_eq);
  and and_1 (and_1_out, not_2_out, IDEX_REGWRITE);
  and and_2 (and_2_out, not_1_out, EXMEM_REGWRITE);
  and and_3 (FA10, and_1_out, comparator_2_eq);
  and and_4 (FB10, and_1_out, comparator_3_eq);
  and and_5 (and_5_out, and_2_out, notA);
  and and_6 (and_6_out, and_2_out, notB);
  and and_7 (FA01, and_5_out, comparator_5_eq);
  and and_8 (FB01, and_6_out, comparator_6_eq);
  not not_3 (notA, FA10);
  not not_4 (notB, FB10);
  Multiplexer multiplexer_1 (.in0(1'b0), .in1(1'b1), .out(ForwardA[0]), .sel(FA01));
  Multiplexer multiplexer_2 (.in0(1'b0), .in1(1'b1), .out(ForwardA[1]), .sel(FA10));
  Multiplexer multiplexer_3 (.in0(1'b0), .in1(1'b1), .out(ForwardB[0]), .sel(FB01));
  Multiplexer multiplexer_4 (.in0(1'b0), .in1(1'b1), .out(ForwardB[1]), .sel(FB10));
endmodule

module FordUnitt (
  input  [4:0] EXMEM_RD,
  input  EXMEM_REGWRITE,
  input  [4:0] IDEX_RS1,
  input  [4:0] IDEX_RS2,
  input  [4:0] MEMWB_RD,
  input  MEMWB_REGWRITE,
  output [1:0] ForwardA,
  output [1:0] ForwardB
);

  wire comparator_1_eq, comparator_2_eq, comparator_3_eq, comparator_4_eq, comparator_5_eq, comparator_6_eq;
  wire [0:0] and_2_out, and_4_out;
  wire [1:1] and_1_out, and_3_out;

  Comparator #(.width(5)) comparator_1 (.a(EXMEM_RD), .b(IDEX_RS1), .eq(comparator_1_eq));  // open: gt, lt
  Comparator #(.width(5)) comparator_2 (.a(IDEX_RS1), .b(MEMWB_RD), .eq(comparator_2_eq));  // open: gt, lt
  Comparator #(.width(5)) comparator_3 (.a(IDEX_RS2), .b(EXMEM_RD), .eq(comparator_3_eq));  // open: gt, lt
  Comparator #(.width(5)) comparator_4 (.a(MEMWB_RD), .b(IDEX_RS2), .eq(comparator_4_eq));  // open: gt, lt
  and and_1 (and_1_out[1], comparator_1_eq, EXMEM_REGWRITE);
  and and_2 (and_2_out[0], comparator_2_eq, MEMWB_REGWRITE);
  and and_3 (and_3_out[1], EXMEM_REGWRITE, comparator_3_eq);
  and and_4 (and_4_out[0], MEMWB_REGWRITE, comparator_4_eq);
  Comparator #(.width(2)) comparator_5 (.a({and_1_out[1], 1'b0}), .b(2'b00), .eq(comparator_5_eq));  // open: gt, lt
  Comparator #(.width(2)) comparator_6 (.a({and_3_out[1], 1'b0}), .b(2'b00), .eq(comparator_6_eq));  // open: gt, lt
  Multiplexer #(.width(2)) multiplexer_1 (
    .in0({and_1_out[1], 1'b0}), .in1({1'b0, and_2_out[0]}), .out(ForwardA), .sel(comparator_5_eq));
  Multiplexer #(.width(2)) multiplexer_2 (
    .in0({and_3_out[1], 1'b0}), .in1({1'b0, and_4_out[0]}), .out(ForwardB), .sel(comparator_6_eq));
endmodule
